# Fritzing sketch scheme (saved by Fritzing 0.9.3b)
breadboards: 1

parts:
  part = Raspberry Pi 2  # not connected
  part_2 = Arduino Uno (Rev3)
  5V_Power_Supply = 4 x AAA Battery Mount
  Finger_Servo_2 = Basic Servo
  Finger_Servo_3 = Basic Servo
  Finger_Servo_1 = Basic Servo
  Thumb_Servo = Basic Servo
  Pressure_Sensor_1 = Basic Force Sensing Resistor (FSR) [package=THT]
  Pressure_Sensor_2 = Basic Force Sensing Resistor (FSR) [package=THT]
  Pressure_Sensor_3 = Basic Force Sensing Resistor (FSR) [package=THT]
  Pressure_Sensor_4 = Basic Force Sensing Resistor (FSR) [package=THT]
  Q1 = PHOTOTRANSISTOR REFLECTIVE OBJECT SENSOR [package=qrb1114-side]
  R1 = Resistor [tolerance=±5% resistance=10k package="0805 [SMD]"]
  R2 = Resistor [tolerance=±5% resistance=200 package="0805 [SMD]"]

nets:
  N1: part_2.A0, Q1.C, R1.Pin_1
  GND: part_2.A1, part_2.A2, part_2.A3, part_2.A4/SDA, Pressure_Sensor_1.pin_1, Pressure_Sensor_2.pin_1, Pressure_Sensor_3.pin_1, Pressure_Sensor_4.pin_1, Q1.E, Q1.K
  N2: part_2.D10_PWM/SS, Thumb_Servo.pulse
  N3: part_2.D3_PWM, Finger_Servo_1.pulse
  N4: part_2.D5_PWM, Finger_Servo_2.pulse
  N5: part_2.D6_PWM, Finger_Servo_3.pulse
  VCC: part_2.5V, Finger_Servo_2.vcc, Finger_Servo_3.vcc, Finger_Servo_1.vcc, Thumb_Servo.vcc, Pressure_Sensor_1.pin_0, Pressure_Sensor_2.pin_0, Pressure_Sensor_3.pin_0, Pressure_Sensor_4.pin_0, R1.Pin_0, R2.Pin_0
  GND_2: part_2.GND, Finger_Servo_2.gnd, Finger_Servo_3.gnd, Finger_Servo_1.gnd, Thumb_Servo.gnd
  Micro USB: 5V_Power_Supply.-, 5V_Power_Supply.+
  N6: Q1.A, R2.Pin_1
